# Fritzing sketch breadboard_fritzing (saved by Fritzing 0.8.3b)
breadboards: 1

parts:
  Part1 = Arduino Pro Mini v13
  U1 = 74HC595 [package="DIP16 [THT]"]
  U2 = 74HC595 [package="DIP16 [THT]"]
  SEG1 = 7-Segment Bubble Display [part_number=COM-12710 package="DIP (Dual Inline) [THT]"]
  R1 = Resistor [tolerance=±5% resistance=330 package=THT]
  R5 = Resistor [tolerance=±5% resistance=330 package=THT]
  R12 = Resistor [tolerance=±5% resistance=330 package=THT]
  Part6 = DeadOn RTC - DS3234 Breakout
  Part7 = OpenLog
  Part8 = Altitude/Pressure Sensor - MPL3115A2 Breakout [part_number=SEN-11084]
  R18 = Resistor [tolerance=±5% resistance=330 package=THT]
  R19 = Resistor [tolerance=±5% resistance=330 package=THT]
  R20 = Resistor [tolerance=±5% resistance=330 package=THT]
  R21 = Resistor [tolerance=±5% resistance=330 package=THT]
  R22 = Resistor [tolerance=±5% resistance=330 package=THT]

nets:
  N1: Part1.A4, Part8.SDA
  N2: Part1.A5, Part8.SCL
  GND: Part1.GND, U1.GND, U2.GND, Part6.GND, Part7.GND
  VCC: Part1.VCC, Part6.VCC, Part7.VCC
  N3: Part1.D13/SCK, Part6.SCLK
  N4: Part1.D12/MISO, Part6.MISO
  N5: Part1.D11_PWM/MOSI, Part6.MOSI
  N6: Part1.D10_PWM/SS, U1.SH_CP, U2.SH_CP
  N7: Part1.D9_PWM, U1.ST_CP, U2.ST_CP
  N8: Part1.D8, U2.DS
  N9: Part1.D7, Part6.SS
  N10: Part1.D2, Part6.INT/SQW
  N11: Part1.D1/RX, Part7.TXO
  N12: Part1.D0/TX, Part7.RXI
  N13: U1.Q1, SEG1.C1
  N14: U1.Q2, SEG1.C3
  N15: U1.Q3, SEG1.C4
  VCC_2: U1.MR, U1.VCC, U2.MR, U2.VCC, Part8.VCC
  N16: U1.OE, U2.OE, Part8.GND
  N17: U1.DS, U2.Q7'
  N18: U1.Q0, SEG1.C2
  N19: U2.Q1, R1.Pin_1
  N20: U2.Q2, R5.Pin_1
  N21: U2.Q3, R12.Pin_1
  N22: U2.Q4, R18.Pin_1
  N23: U2.Q5, R19.Pin_1
  N24: U2.Q6, R20.Pin_1
  N25: U2.Q7, R21.Pin_1
  N26: U2.Q0, R22.Pin_1
  N27: SEG1.Ae, R1.Pin_0
  N28: SEG1.Ac, R5.Pin_0
  N29: SEG1.Adp, R12.Pin_0
  N30: SEG1.Ag, R21.Pin_0
  N31: SEG1.Ad, R20.Pin_0
  N32: SEG1.Af, R19.Pin_0
  N33: SEG1.Ab, R18.Pin_0
  N34: SEG1.Aa, R22.Pin_0

custom parts:
  7-Segment Bubble Display: This is the HP QDSP-6064 bubble display, a tiny, 4-digit, 7-segment numerical indicator. THis little guy is perfect if you need some user feedback from your system, but don’t want to fiddle with LCDs or other display options. The Bubble Display comes in an easy-to-use 12-pin DIP package and can be used in breadboards, protoboards, or PCBs.
  Altitude/Pressure Sensor - MPL3115A2 Breakout: Life has its ups and downs, so why not measure them? The MPL3115A2 is a MEMS pressure sensor that provides Altitude data to within 30cm (with oversampling enabled). The sensor outputs are digitized by a high resolution 24-bit ADC and transmitted over I2C, meaning it's easy to interface with most controllers. Pressure output can be resolved with output in fractions of a Pascal, and Altitude can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
